// Logisim project BABY.circ as structural Verilog: 1 circuit, main circuit main
module main (
  input  [31:0] ram_data_i,
  input  reset_i,
  output [4:0] ram_addr_o,
  output [31:0] ram_data_o,
  output ram_rw_en_o,
  output stop_lamp_o,
  output clock_o
);

  wire and_1_out, and_2_out, and_3_out, and_4_out, and_5_out, and_6_out, and_7_out, and_8_out, and_9_out,
       and_11_out, and_12_out, decoder_1_out4, decoder_1_out5, HLT, JMP, JRP, LDN, or_2_out, or_4_out,
       or_6_out, or_7_out, s_r_ff_1_qn, SKN, STO, SUB, t0, t1, t2, t3, t4, t5, t6, t7;
  wire [0:0] comparator_1_lt;
  wire [2:0] counter_1_q;
  wire [4:0] adder_1_out, adder_2_out, adder_3_out, multiplexer_3_out, multiplexer_4_out, multiplexer_5_out,
       multiplexer_6_out, multiplexer_7_out, multiplexer_8_out, multiplexer_9_out, multiplexer_10_out,
       multiplexer_11_out, multiplexer_12_out, or_5_out, PC_q;
  wire [31:0] IR_q, multiplexer_1_out, multiplexer_2_out, or_1_out, subtractor_1_out, subtractor_2_out;

  Clock clock_1 (.out(clock_o));
  Subtractor #(.width(32)) subtractor_1 (.a({32{1'b0}}), .b(ram_data_i), .out(subtractor_1_out));  // open: bin, bout
  Subtractor #(.width(32)) subtractor_2 (.a(ram_data_o), .b(ram_data_i), .out(subtractor_2_out));  // open: bin, bout
  Register #(.width(32)) IR (.D(ram_data_i), .en(t2), .clk(clock_o), .Q(IR_q), .clr(reset_i));
  and and_1 (and_1_out, t4, LDN);
  and and_2 (and_2_out, t4, SUB);
  Multiplexer #(.width(32)) multiplexer_1 (
    .in0({32{1'b0}}), .in1(subtractor_1_out), .out(multiplexer_1_out), .sel(and_1_out));
  Multiplexer #(.width(32)) multiplexer_2 (
    .in0({32{1'b0}}), .in1(subtractor_2_out), .out(multiplexer_2_out), .sel(and_2_out));
  Decoder #(.select(3)) decoder_1 (
    .out0(JMP), .out1(JRP), .out2(LDN), .out3(STO), .out4(decoder_1_out4), .out5(decoder_1_out5), .out6(SKN),
    .out7(HLT), .sel(IR_q[15:13]));  // open: en
  and and_3 (and_3_out, HLT, t4);
  Register #(.width(32)) Acc (.D(or_1_out), .en(or_2_out), .clk(clock_o), .Q(ram_data_o), .clr(reset_i));
  assign or_1_out = multiplexer_1_out | multiplexer_2_out;  // OR_Gate or_1, 32 bits wide
  or or_2 (or_2_out, and_1_out, and_2_out);
  S_R_Flip_Flop s_r_ff_1 (
    .S(and_3_out), .R(1'b0), .clk(clock_o), .Q(stop_lamp_o), .reset(reset_i), .Qn(s_r_ff_1_qn));  // open: preset
  or or_3 (SUB, decoder_1_out4, decoder_1_out5);
  Comparator #(.width(32)) comparator_1 (.a(ram_data_o), .b({32{1'b0}}), .lt(comparator_1_lt[0]));  // open: gt, eq
  Adder #(.width(5)) adder_1 (.a(ram_data_i[4:0]), .b(PC_q), .out(adder_1_out));  // open: cin, cout
  Counter #(.max('h7), .width(3)) counter_1 (
    .clr(reset_i), .up(1'b1), .clk(and_4_out), .Q(counter_1_q));  // open: load, count, D, carry
  and and_4 (and_4_out, clock_o, s_r_ff_1_qn);
  or or_4 (or_4_out, SUB, LDN, STO);
  Multiplexer #(.width(5)) multiplexer_3 (.in0({5{1'b0}}), .in1(adder_2_out), .out(multiplexer_3_out), .sel(t0));
  Adder #(.width(5)) adder_2 (.a(5'b00001), .b(PC_q), .out(adder_2_out));  // open: cin, cout
  Multiplexer #(.width(5)) multiplexer_4 (
    .in0({5{1'b0}}), .in1(ram_data_i[4:0]), .out(multiplexer_4_out), .sel(and_5_out));
  and and_5 (and_5_out, JMP, t5);
  Multiplexer #(.width(5)) multiplexer_5 (.in0({5{1'b0}}), .in1(adder_3_out), .out(multiplexer_5_out), .sel(and_6_out));
  Adder #(.width(5)) adder_3 (.a(PC_q), .b({4'b0000, comparator_1_lt[0]}), .out(adder_3_out));  // open: cin, cout
  and and_6 (and_6_out, SKN, t5);
  Multiplexer #(.width(5)) multiplexer_6 (.in0({5{1'b0}}), .in1(adder_1_out), .out(multiplexer_6_out), .sel(and_7_out));
  and and_7 (and_7_out, JRP, t5);
  Multiplexer #(.width(5)) multiplexer_7 (.in0({5{1'b0}}), .in1(PC_q), .out(multiplexer_7_out), .sel(and_8_out));
  and and_8 (and_8_out, or_4_out, t5);
  Decoder #(.select(3)) decoder_2 (
    .out0(t0), .out1(t1), .out2(t2), .out3(t3), .out4(t4), .out5(t5), .out6(t6), .out7(t7), .sel(counter_1_q));  // open: en
  assign or_5_out = multiplexer_3_out | multiplexer_4_out | multiplexer_5_out | multiplexer_6_out | multiplexer_7_out;  // OR_Gate or_5, 5 bits wide
  or or_6 (or_6_out, t0, t5);
  Register #(.width(5)) PC (.D(or_5_out), .en(or_6_out), .clk(clock_o), .Q(PC_q), .clr(reset_i));
  or or_7 (or_7_out, JMP, JRP);
  Multiplexer #(.width(5)) multiplexer_8 (.in0({5{1'b0}}), .in1(PC_q), .out(multiplexer_8_out), .sel(t1));
  Multiplexer #(.width(5)) multiplexer_9 (.in0({5{1'b0}}), .in1(IR_q[4:0]), .out(multiplexer_9_out), .sel(and_9_out));
  and and_9 (and_9_out, t3, LDN);
  Multiplexer #(.width(5)) multiplexer_10 (
    .in0({5{1'b0}}), .in1(IR_q[4:0]), .out(multiplexer_10_out), .sel(ram_rw_en_o));
  and and_10 (ram_rw_en_o, t3, STO);
  Multiplexer #(.width(5)) multiplexer_11 (
    .in0({5{1'b0}}), .in1(IR_q[4:0]), .out(multiplexer_11_out), .sel(and_11_out));
  and and_11 (and_11_out, t3, SUB);
  Multiplexer #(.width(5)) multiplexer_12 (
    .in0({5{1'b0}}), .in1(IR_q[4:0]), .out(multiplexer_12_out), .sel(and_12_out));
  and and_12 (and_12_out, t4, or_7_out);
  assign ram_addr_o = multiplexer_8_out | multiplexer_9_out | multiplexer_10_out | multiplexer_11_out | multiplexer_12_out;  // OR_Gate or_8, 5 bits wide

  // Other names for the same wires on the sheet: clk = clock_o; reset = reset_i

  // Notes on the sheet:
  //   Clock
  //   Stop lamp
  //   data to ram
  //   data from ram
endmodule
